// Logisim project assign1bonus.circ as structural Verilog: 8 circuits, main circuit main
module main (
);

  wire a_1_out_5, b_1_out_5, button_1_out, c_1_out_5, d_1_out_5, e_1_out_5, f_1_out_5, g_1_out_5;
  wire [3:0] counter_1_q;

  Button button_1 (.out(button_1_out));
  Counter #(.width(4), .max('hf)) counter_1 (.Q(counter_1_q), .clk(button_1_out));  // open: load, D, count, carry, clr
  A a_1 (.W(counter_1_q[3]), .X(counter_1_q[2]), .Y(counter_1_q[1]), .Z(counter_1_q[0]), .out_5(a_1_out_5));
  B b_1 (.W(counter_1_q[3]), .X(counter_1_q[2]), .Y(counter_1_q[1]), .Z(counter_1_q[0]), .out_5(b_1_out_5));
  C c_1 (.W(counter_1_q[3]), .X(counter_1_q[2]), .Y(counter_1_q[1]), .Z(counter_1_q[0]), .out_5(c_1_out_5));
  D d_1 (.W(counter_1_q[3]), .X(counter_1_q[2]), .Y(counter_1_q[1]), .Z(counter_1_q[0]), .out_5(d_1_out_5));
  E e_1 (.W(counter_1_q[3]), .X(counter_1_q[2]), .Y(counter_1_q[1]), .Z(counter_1_q[0]), .out_5(e_1_out_5));
  F f_1 (.W(counter_1_q[3]), .X(counter_1_q[2]), .Y(counter_1_q[1]), .Z(counter_1_q[0]), .out_5(f_1_out_5));
  G g_1 (.W(counter_1_q[3]), .X(counter_1_q[2]), .Y(counter_1_q[1]), .Z(counter_1_q[0]), .out_5(g_1_out_5));
  _7_Segment_Display u_7_segment_display_1 (
    .g(g_1_out_5), .f(f_1_out_5), .a(a_1_out_5), .b(b_1_out_5), .e(e_1_out_5), .d(d_1_out_5), .c(c_1_out_5));  // open: dp
endmodule

module A (
  input  W,
  input  X,
  input  Y,
  input  Z,
  output out_5
);

  wire and_1_out, and_2_out, and_3_out, and_4_out, and_5_out, and_6_out, not_1_out, not_2_out, not_3_out,
       not_4_out;

  not not_1 (not_1_out, W);
  not not_2 (not_2_out, X);
  not not_3 (not_3_out, Y);
  not not_4 (not_4_out, Z);
  and and_1 (and_1_out, not_2_out, not_4_out);
  and and_2 (and_2_out, not_1_out, Y);
  and and_3 (and_3_out, X, Y);
  and and_4 (and_4_out, W, not_4_out);
  and and_5 (and_5_out, not_1_out, X, Z);
  and and_6 (and_6_out, W, not_2_out, not_3_out);
  or or_1 (out_5, and_1_out, and_2_out, and_3_out, and_4_out, and_5_out, and_6_out);
endmodule

module B (
  input  W,
  input  X,
  input  Y,
  input  Z,
  output out_5
);

  wire and_1_out, and_2_out, and_3_out, and_4_out, and_5_out, not_1_out, not_2_out, not_3_out, not_4_out;

  not not_1 (not_1_out, W);
  not not_2 (not_2_out, X);
  not not_3 (not_3_out, Y);
  not not_4 (not_4_out, Z);
  and and_1 (and_1_out, not_2_out, not_4_out);
  and and_2 (and_2_out, not_1_out, not_2_out);
  and and_3 (and_3_out, not_1_out, not_3_out, not_4_out);
  and and_4 (and_4_out, not_1_out, Y, Z);
  and and_5 (and_5_out, W, not_3_out, Z);
  or or_1 (out_5, and_1_out, and_2_out, and_3_out, and_4_out, and_5_out);
endmodule

module C (
  input  W,
  input  X,
  input  Y,
  input  Z,
  output out_5
);

  wire and_1_out, and_2_out, and_3_out, and_4_out, and_5_out, not_1_out, not_2_out, not_3_out;

  not not_1 (not_1_out, W);
  not not_2 (not_2_out, X);
  not not_3 (not_3_out, Y);
  and and_1 (and_1_out, not_1_out, X);
  and and_2 (and_2_out, W, not_2_out);
  and and_3 (and_3_out, not_3_out, Z);
  and and_4 (and_4_out, not_1_out, not_3_out);
  and and_5 (and_5_out, not_1_out, Z);
  or or_1 (out_5, and_1_out, and_2_out, and_3_out, and_4_out, and_5_out);
endmodule

module D (
  input  W,
  input  X,
  input  Y,
  input  Z,
  output out_5
);

  wire and_1_out, and_2_out, and_3_out, and_4_out, and_5_out, not_1_out, not_2_out, not_3_out, not_4_out;

  not not_1 (not_1_out, W);
  not not_2 (not_2_out, X);
  not not_3 (not_3_out, Y);
  not not_4 (not_4_out, Z);
  and and_1 (and_1_out, not_2_out, Y, Z);
  and and_2 (and_2_out, not_1_out, not_2_out, not_4_out);
  and and_3 (and_3_out, X, Y, not_4_out);
  and and_4 (and_4_out, X, not_3_out, Z);
  and and_5 (and_5_out, W, not_3_out);
  or or_1 (out_5, and_1_out, and_2_out, and_3_out, and_4_out, and_5_out);
endmodule

module E (
  input  W,
  input  X,
  input  Y,
  input  Z,
  output out_5
);

  wire and_1_out, and_2_out, and_3_out, and_4_out, not_1_out, not_2_out;

  not not_1 (not_1_out, X);
  not not_2 (not_2_out, Z);
  and and_1 (and_1_out, Y, not_2_out);
  and and_2 (and_2_out, W, X);
  and and_3 (and_3_out, not_1_out, not_2_out);
  and and_4 (and_4_out, W, Y);
  or or_1 (out_5, and_1_out, and_2_out, and_3_out, and_4_out);
endmodule

module F (
  input  W,
  input  X,
  input  Y,
  input  Z,
  output out_5
);

  wire and_1_out, and_2_out, and_3_out, and_4_out, and_5_out, not_1_out, not_2_out, not_3_out, not_4_out;

  not not_1 (not_1_out, W);
  not not_2 (not_2_out, X);
  not not_3 (not_3_out, Y);
  not not_4 (not_4_out, Z);
  and and_1 (and_1_out, not_3_out, not_4_out);
  and and_2 (and_2_out, W, not_2_out);
  and and_3 (and_3_out, W, Y);
  and and_4 (and_4_out, not_1_out, X, not_3_out);
  and and_5 (and_5_out, X, not_4_out);
  or or_1 (out_5, and_1_out, and_2_out, and_3_out, and_4_out, and_5_out);
endmodule

module G (
  input  W,
  input  X,
  input  Y,
  input  Z,
  output out_5
);

  wire and_1_out, and_2_out, and_3_out, and_4_out, and_5_out, not_1_out, not_2_out, not_3_out, not_4_out;

  not not_1 (not_1_out, W);
  not not_2 (not_2_out, X);
  not not_3 (not_3_out, Y);
  not not_4 (not_4_out, Z);
  and and_1 (and_1_out, Y, not_4_out);
  and and_2 (and_2_out, not_2_out, Y);
  and and_3 (and_3_out, not_1_out, X, not_3_out);
  and and_4 (and_4_out, W, not_2_out);
  and and_5 (and_5_out, W, Z);
  or or_1 (out_5, and_1_out, and_2_out, and_3_out, and_4_out, and_5_out);
endmodule
