// Logisim project assign2bonus.circ as structural Verilog: 1 circuit, main circuit main
module main (
  input  in_1,
  input  in_2
);

  wire A_q, and_1_out, and_2_out, and_3_out, and_4_out, and_5_out, and_6_out, and_7_out, and_8_out,
       and_9_out, and_10_out, and_11_out, and_12_out, and_13_out, and_14_out, and_15_out, and_16_out, B_q,
       C_q, clock_1_out, not_1_out, not_2_out, not_3_out, not_4_out, not_5_out, or_1_out, or_2_out, or_3_out;

  not not_1 (not_1_out, B_q);
  not not_2 (not_2_out, A_q);
  not not_3 (not_3_out, C_q);
  not not_4 (not_4_out, in_1);
  not not_5 (not_5_out, in_2);
  and and_1 (and_1_out, not_2_out, not_1_out, not_3_out, in_1, in_2);
  and and_2 (and_2_out, not_2_out, B_q, not_3_out, not_4_out, in_2);
  and and_3 (and_3_out, A_q, not_1_out, not_3_out, not_4_out, in_2);
  and and_4 (and_4_out, A_q, B_q, not_3_out, in_1, in_2);
  and and_5 (and_5_out, not_2_out, not_1_out, C_q, not_4_out, in_2);
  and and_6 (and_6_out, not_2_out, B_q, C_q, in_1, in_2);
  and and_7 (and_7_out, A_q, not_1_out, C_q, in_1, in_2);
  and and_8 (and_8_out, A_q, B_q, C_q, not_4_out, in_2);
  and and_9 (and_9_out, not_2_out, not_1_out, not_3_out, not_4_out, in_2);
  and and_10 (and_10_out, not_2_out, not_1_out, C_q, in_1, in_2);
  and and_11 (and_11_out, not_2_out, B_q, not_3_out, in_1, in_2);
  and and_12 (and_12_out, not_2_out, B_q, C_q, not_4_out, in_2);
  and and_13 (and_13_out, A_q, not_1_out, not_3_out, in_1, in_2);
  and and_14 (and_14_out, A_q, not_1_out, C_q, not_4_out, in_2);
  and and_15 (and_15_out, A_q, B_q, not_3_out, not_4_out, in_2);
  and and_16 (and_16_out, A_q, B_q, C_q, in_1, in_2);
  or or_1 (or_1_out, and_1_out, and_2_out, and_3_out, and_4_out);
  or or_2 (or_2_out, and_5_out, and_6_out, and_7_out, and_8_out);
  or or_3 (or_3_out, and_9_out, and_10_out, and_11_out, and_12_out, and_13_out, and_14_out, and_15_out, and_16_out);
  Clock clock_1 (.out(clock_1_out));
  T_Flip_Flop A (.clk(clock_1_out), .T(or_1_out), .Q(A_q));  // open: Qn, preset, reset, en
  T_Flip_Flop B (.clk(clock_1_out), .T(or_2_out), .Q(B_q));  // open: Qn, preset, reset, en
  T_Flip_Flop C (.clk(clock_1_out), .T(or_3_out), .Q(C_q));  // open: Qn, preset, reset, en
  LED led_1 (.in(A_q));
  LED led_2 (.in(B_q));
  LED led_3 (.in(C_q));
endmodule
